# Fritzing sketch Fritzing (saved by Fritzing 0.9.2b)
breadboards: 1

parts:
  Netduino1 = Netduino
  LED1 = smd LED [color="Red (633nm)" package="1206 [SMD]"]
  R1 = Resistor [tolerance=±5% resistance=220 package=THT]
  S1 = Pushbutton [package="[THT]"]
  R2 = Resistor [tolerance=±5% resistance=220 package=THT]

nets:
  N1: Netduino1.D13_SPCK, R1.Pin_1
  N2: Netduino1.D2_RX1, S1.Pin_3, S1.Pin_4, R2.Pin_1
  N3: Netduino1.+5V, S1.Pin_1, S1.Pin_2, R2.Pin_0
  N4: Netduino1.GND, LED1.cathode
  N5: LED1.anode, R1.Pin_0
